// Digital circuit Project_Potato.dig as structural Verilog
module Project_Potato (
  input  clk,
  input  in_2,
  input  in_3,
  input  in_4,
  input  in_5,
  input  in_6,
  input  in_7,
  input  in_8,
  input  in_9,
  input  in_10,
  input  in_11,
  input  in_12,
  input  [3:0] in_13,
  input  in_14
);

  wire _7448_1_p10, _7448_1_p11, _7448_1_p12, _7448_1_p13, _7448_1_p14, _7448_1_p15, _7448_1_p16,
       decoder_1_out_1, decoder_1_out_2, decoder_1_out_3, decoder_1_out_4, decoder_1_out_5, decoder_1_out_6,
       decoder_1_out_7, delay_1_out, Halt_Command, multiplexer_1_out, multiplexer_2_out, R_out, xor_1_out;
  wire [3:0] add_1_s, cache_q, counterpreset_1_out, DisplayReg_q, multiplexer_3_out, multiplexer_4_out,
       RegA_q, RegB_q, sub_1_s;
  wire [7:0] rom_1_d;

  Multiplexer multiplexer_1 (.sel(Halt_Command), .in_0(in_2), .in_1(in_3), .out(multiplexer_1_out));
  Button R (.out(R_out));
  LED led_1 (.in(counterpreset_1_out[3]));
  LED led_2 (.in(counterpreset_1_out[2]));
  LED led_3 (.in(counterpreset_1_out[1]));
  CounterPreset #(.Bits(4)) counterpreset_1 (
    .en(multiplexer_1_out), .C(clk), .dir(in_12), .in(in_13), .ld(decoder_1_out_5), .clr(R_out),
    .out(counterpreset_1_out));  // open: ovf
  LED led_4 (.in(counterpreset_1_out[0]));
  ROM #(.AddrBits(4), .Bits(8)) rom_1 (.A(counterpreset_1_out), .sel(in_5), .D(rom_1_d));
  LED led_5 (.in(rom_1_d[7]));
  LED led_6 (.in(rom_1_d[6]));
  LED led_7 (.in(rom_1_d[5]));
  LED led_8 (.in(rom_1_d[4]));
  LED led_9 (.in(rom_1_d[3]));
  LED led_10 (.in(rom_1_d[2]));
  LED led_11 (.in(rom_1_d[1]));
  LED led_12 (.in(rom_1_d[0]));
  Decoder #(.Selector_Bits(4)) decoder_1 (
    .sel(rom_1_d[7:4]), .out_1(decoder_1_out_1), .out_2(decoder_1_out_2), .out_3(decoder_1_out_3),
    .out_4(decoder_1_out_4), .out_5(decoder_1_out_5), .out_6(decoder_1_out_6), .out_7(decoder_1_out_7),
    .out_15(Halt_Command));  // open: out_0, out_8, out_9, out_10, out_11, out_12, out_13, out_14
  Register #(.Bits(4)) RegA (.D(rom_1_d[3:0]), .C(decoder_1_out_1), .en(in_4), .Q(RegA_q));
  Multiplexer multiplexer_2 (
    .sel(decoder_1_out_6), .in_0(decoder_1_out_4), .in_1(decoder_1_out_6), .out(multiplexer_2_out));
  xor xor_1 (xor_1_out, decoder_1_out_4, decoder_1_out_6);
  Multiplexer #(.Bits(4)) multiplexer_3 (
    .sel(multiplexer_2_out), .in_0(rom_1_d[3:0]), .in_1(cache_q), .out(multiplexer_3_out));
  Register #(.Bits(4)) RegB (.D(multiplexer_3_out), .C(delay_1_out), .en(in_8), .Q(RegB_q));
  Delay delay_1 (.in(xor_1_out), .out(delay_1_out));
  Add #(.Bits(4)) add_1 (.a(RegB_q), .b(RegA_q), .c_i(in_9), .s(add_1_s));  // open: c_o
  Sub #(.Bits(4)) sub_1 (.a(RegB_q), .b(RegA_q), .c_i(in_10), .s(sub_1_s));  // open: c_o
  Multiplexer #(.Bits(4)) multiplexer_4 (
    .sel(decoder_1_out_2), .in_0(add_1_s), .in_1(sub_1_s), .out(multiplexer_4_out));
  Register #(.Bits(4)) cache (.D(multiplexer_4_out), .C(decoder_1_out_7), .en(in_14), .Q(cache_q));
  Register #(.Bits(4)) DisplayReg (.D(multiplexer_4_out), .C(decoder_1_out_3), .en(in_11), .Q(DisplayReg_q));
  // _7448 _7448_1: pin names not known; wires that end beside it: in_6, in_7, DisplayReg_q[0], DisplayReg_q[1], DisplayReg_q[2], DisplayReg_q[3], in_6, in_6, in_6, _7448_1_p10, _7448_1_p11, _7448_1_p12, _7448_1_p13, _7448_1_p14, _7448_1_p15, _7448_1_p16
  Seven_Seg seven_seg_1 (
    .a(_7448_1_p10), .b(_7448_1_p11), .c(_7448_1_p12), .d(_7448_1_p13), .e(_7448_1_p14), .f(_7448_1_p15),
    .g(_7448_1_p16), .dp(in_7));

  // Notes on the sheet:
  //   in_2: default 1
  //   in_4: default 1
  //   in_5: default 1
  //   in_6: default 1
  //   in_8: default 1
  //   in_11: default 1
  //   in_14: default 1
  //   contents of rom_1 (hex, n*v repeats v):
  //   12,42,0,70,60,0,70,60,0,70,60,0,70,30,f0,f0
endmodule
